# Fritzing sketch gardnero_wiring (saved by Fritzing 0.9.4)
breadboards: 1

parts:
  MCU1 = Raspberry Pi Zero
  KY-1 = Keyes Relay [package=THT]
  Power_plug1 = Power plug
  HLK-PM2 = HLK-PM01
  S1 = Taiway 100-SP-X-T1 SPDT Miniature Toggle Switch [part_number=100-SP-X-T1-0-0-B1-M1 package=THT]
  HLK-PM1 = HLK-PM12 [part_number=HLK-PM12]
  S2 = Pushbutton [package="[SMD]"]
  LED1 = smd LED [color="Red (633nm)" package="1206 [SMD]"]
  LED2 = smd LED [color="Red (633nm)" package="1206 [SMD]"]
  LED3 = smd LED [color="Red (633nm)" package="1206 [SMD]"]
  KY-2 = Keyes Relay [package=THT]
  KY-3 = Keyes Relay [package=THT]
  KY-4 = Keyes Relay [package=THT]
  M2 = DC Motor
  M3 = DC Motor
  M1 = DC Motor

nets:
  N1: MCU1.pin_2, MCU1.pin_4, KY-1.power, HLK-PM2.+Vo
  N2: MCU1.pin_6, MCU1.pin_20, MCU1.pin_34, KY-1.ground, HLK-PM2.-Vo, S2.Pin_3, S2.Pin_4, LED1.cathode, LED2.cathode, LED3.cathode
  N3: MCU1.pin_7, KY-1.signal
  N4: MCU1.pin_31, LED1.anode
  N5: MCU1.pin_33, LED3.anode
  N6: MCU1.pin_35, LED2.anode
  N7: MCU1.pin_36, KY-4.signal
  N8: MCU1.pin_37, S2.Pin_1, S2.Pin_2
  N9: MCU1.pin_40, KY-2.signal
  N10: KY-1.C, HLK-PM2.AC#0, S1.L1
  N11: KY-1.NO, HLK-PM1.AC_2
  N12: Power_plug1.GND, HLK-PM2.AC#1, HLK-PM1.AC_1
  N13: Power_plug1.VCC, S1.L2
  N14: HLK-PM1.-Vo, M2.pin_1, M3.pin_1, M1.pin_1
  N15: HLK-PM1.+Vo, KY-2.C, KY-3.C, KY-4.C
  N16: KY-2.NO, M1.pin_2
  N17: KY-3.NO, M2.pin_2
  N18: KY-4.NO, M3.pin_2

custom parts:
  Keyes Relay: The Keyes 5V relay module is suitable for SCM development, home appliance control. It uses a 5V~12V TIL control signal which can control DC / AC signal.
